# Fritzing sketch engine_test_setup (saved by Fritzing 0.9.3b)
breadboards: 1

parts:
  Part1 = Arduino Uno (Rev3)
  M1 = DC Motor
  M2 = DC Motor
  R2 = Resistor [tolerance=±5% resistance=5.3k package=THT]
  MD03A1 = Dual VNH2SP30 Motor Driver [part_number=MD03A]
  U1 = LIPO-1000mAh [package=lipo-1000]
  hc-sr1 = hc-sr04
  R3 = Rotary Potentiometer (Small) [maximum_resistance=100kΩ package=THT]

nets:
  N1: Part1.A0, R2.Pin_0, R3.leg2
  N2: Part1.D8, MD03A1.2INb#142
  N3: Part1.D12/MISO, MD03A1.2INb#143
  N4: Part1.D2, MD03A1.1INa
  N5: Part1.D3_PWM, MD03A1.PWM
  N6: Part1.D4, hc-sr1.Echo
  N7: Part1.D5_PWM, MD03A1.2PWM
  N8: Part1.D6_PWM, hc-sr1.Trig
  N9: Part1.D7, MD03A1.1INb
  N10: M1.pin_1, MD03A1.OUT_1A
  N11: M1.pin_2, MD03A1.OUT_1B
  N12: M2.pin_1, MD03A1.OUT_2A
  N13: M2.pin_2, MD03A1.OUT_2B
  N14: R2.Pin_1, MD03A1.GND#136, hc-sr1.GND
  N15: MD03A1.+5V_(IN), hc-sr1.VCC, R3.leg1
  N16: MD03A1.VIN, U1.+
  N17: MD03A1.GND#151, U1.-
