# Fritzing sketch system_setup (saved by Fritzing 0.9.3b)
breadboards: 1

parts:
  Part1 = Arduino Uno (Rev3)
  M1 = DC Motor
  M2 = DC Motor
  R2 = Resistor [tolerance=±5% resistance=5.3k package=THT]
  hc-sr1 = hc-sr04
  R3 = Rotary Potentiometer (Small) [maximum_resistance=100kΩ package=THT]
  Part2 = Adafruit TB6612 DC and Stepper Motor Driver [part_number="Adafruit #2448"]
  Raspberry_Pi_Zero1 = Raspberry Pi Zero
  Part3 = Adafruit 4-channel I2C-safe Bi-directional Logic Level Converter [part_number="Adafruit #757"]
  BAT1 = BATTERY-2 [package=battery-aa]
  BAT2 = BATTERY-2 [package=battery-aa]
  BAT3 = BATTERY-2 [package=battery-aa]
  BAT4 = BATTERY-2 [package=battery-aa]
  BAT5 = BATTERY-2 [package=battery-aa]
  BAT6 = BATTERY-2 [package=battery-aa]  # not connected
  BAT6_2 = BATTERY-2 [package=battery-aa]

nets:
  N1: Part1.A0, R2.Pin_1, R3.leg1
  N2: Part1.D8, Part2.BIN1
  N3: Part1.D9_PWM, hc-sr1.Echo
  N4: Part1.D12/MISO, Part2.BIN2
  N5: Part1.D0/RX, Part3.B1
  N6: Part1.D1/TX, Part3.B2
  N7: Part1.D2, Part2.AIN1
  N8: Part1.D3_PWM, Part2.PWMA
  N9: Part1.D4, Part2.STBY
  N10: Part1.D5_PWM, Part2.PWMB
  N11: Part1.D6_PWM, hc-sr1.Trig
  N12: Part1.D7, Part2.AIN2
  5V: Part1.5V, hc-sr1.VCC, R3.leg2, Part2.VCC, Raspberry_Pi_Zero1.5V
  GND: Part1.GND, R2.Pin_0, hc-sr1.GND, Part2.GND, Raspberry_Pi_Zero1.GND, Part3.GND, BAT1.+1
  N13: M1.pin_1, Part2.MOTORB1
  N14: M1.pin_2, Part2.MOTORB2
  N15: M2.pin_1, Part2.MOTORA2
  N16: M2.pin_2, Part2.MOTORA1
  N17: Part2.Vmotor, BAT6_2.-1
  N18: Raspberry_Pi_Zero1.GPIO15, Part3.A2
  N19: Raspberry_Pi_Zero1.GPIO14, Part3.A1
  N20: BAT1.-1, BAT2.+1
  N21: BAT2.-1, BAT3.+1
  N22: BAT3.-1, BAT4.+1
  N23: BAT4.-1, BAT5.+1

custom parts:
  Adafruit TB6612 DC and Stepper Motor Driver: Spin two DC motors, step one bi-polar or uni-polar stepper, or fire off two solenoids with 1.2A per channel using the TB6612. These are perhaps better known as "the drivers in our assembled Adafruit Motorshield or Motor HAT." We really like these dual H-bridges, so if you want to control motors without a shield or HAT these are easy to include on any solderless breadboard or perma-proto.
  Adafruit 4-channel I2C-safe Bi-directional Logic Level Converter: Because the Arduino (and Basic Stamp) are 5V devices, and most modern sensors, displays, flash cards and modes are 3.3V-only, many makers find that they need to perform level shifting/conversion to protect the 3.3V device from 5V. We do have some other handy level shifters in the shop, from the DIP 74LVC245 to the fancy bi-directional TXB0108. However, neither of these are happy to work with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
