# Fritzing sketch system_setup_new (saved by Fritzing 0.9.3b)
breadboards: 1

parts:
  Part1 = Adafruit Pro Trinket 5V 16MHz [part_number="Adafruit #2000"]
  Part2 = Adafruit 4-channel I2C-safe Bi-directional Logic Level Converter [part_number="Adafruit #757"]
  Part3 = Adafruit TB6612 DC and Stepper Motor Driver [part_number="Adafruit #2448"]
  R1 = Rotary Potentiometer (Small) [maximum_resistance=100kΩ package=THT]
  R2 = Resistor [tolerance=±5% resistance=5.3k package="0603 [SMD]"]
  M1 = DC Motor
  M2 = DC Motor
  BAT7 = BATTERY-2 [package=battery-aa]
  BAT8 = BATTERY-2 [package=battery-aa]
  BAT9 = BATTERY-2 [package=battery-aa]
  BAT10 = BATTERY-2 [package=battery-aa]
  BAT11 = BATTERY-2 [package=battery-aa]
  BAT12 = BATTERY-2 [package=battery-aa]
  BAT13 = BATTERY-2 [package=battery-aa]
  Raspberry_Pi_Zero1 = Raspberry Pi Zero
  hc-sr2 = hc-sr04

nets:
  GND: Part1.GND, Part2.GND, Part3.GND, R2.Pin_0, BAT7.-1, BAT8.-1, Raspberry_Pi_Zero1.GND, hc-sr2.GND
  VCC: Part1.+5V, Part2.HV, Part3.VCC, R1.leg2, hc-sr2.VCC
  N1: Part1.D8, Part3.BIN1
  N2: Part1.D6, Part3.AIN1
  N3: Part1.D5, Part3.AIN2
  N4: Part1.D4, Part3.STBY
  N5: Part1.D3, Part3.PWMA
  N6: Part1.TXD, Part2.B2
  N7: Part1.RXD, Part2.B1
  N8: Part1.D9, Part3.PWMB
  N9: Part1.D10, Part3.BIN2
  N10: Part1.D11, hc-sr2.Trig
  N11: Part1.D12, hc-sr2.Echo
  N12: Part1.A0, R1.leg1, R2.Pin_1
  N13: Part2.A2, Raspberry_Pi_Zero1.GPIO15
  N14: Part2.A1, Raspberry_Pi_Zero1.GPIO14
  N15: Part2.LV, Raspberry_Pi_Zero1.3v3
  N16: Part3.Vmotor, Part3.PWRIN, BAT13.+1
  N17: Part3.MOTORA1, M2.pin_2
  N18: Part3.MOTORA2, M2.pin_1
  N19: Part3.MOTORB2, M1.pin_2
  N20: Part3.MOTORB1, M1.pin_1
  N21: BAT7.+1, BAT8.+1, BAT9.-1
  N22: BAT9.+1, BAT10.-1
  N23: BAT10.+1, BAT11.-1
  N24: BAT11.+1, BAT12.-1
  N25: BAT12.+1, BAT13.-1

custom parts:
  Adafruit Pro Trinket 5V 16MHz: Trinket's got a big sister in town - the Pro Trinket 5V! Pro Trinket combines everything you love about Trinket with the familiarity of the common core Arduino chip, the ATmega328. It's like an Arduino Pro Mini with more pins and USB tossed in, so delicious. Trinket's a year old now, and while its been great to see tons of tiny projects, sometimes you just need more pins, more FLASH, and more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
  Adafruit 4-channel I2C-safe Bi-directional Logic Level Converter: Because the Arduino (and Basic Stamp) are 5V devices, and most modern sensors, displays, flash cards and modes are 3.3V-only, many makers find that they need to perform level shifting/conversion to protect the 3.3V device from 5V. We do have some other handy level shifters in the shop, from the DIP 74LVC245 to the fancy bi-directional TXB0108. However, neither of these are happy to work with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
  Adafruit TB6612 DC and Stepper Motor Driver: Spin two DC motors, step one bi-polar or uni-polar stepper, or fire off two solenoids with 1.2A per channel using the TB6612. These are perhaps better known as "the drivers in our assembled Adafruit Motorshield or Motor HAT." We really like these dual H-bridges, so if you want to control motors without a shield or HAT these are easy to include on any solderless breadboard or perma-proto.
