# Fritzing sketch engine_test_setup (saved by Fritzing 0.9.3b)
breadboards: 1

parts:
  Part1 = Arduino Uno (Rev3)
  M1 = DC Motor
  M2 = DC Motor
  R1 = Rotary Potentiometer (Small) [maximum_resistance=100kΩ package=THT]
  R2 = Resistor [tolerance=±5% resistance=5.3k package=THT]
  MD03A1 = Dual VNH2SP30 Motor Driver [part_number=MD03A]
  U1 = LIPO-1000mAh [package=lipo-1000]

nets:
  N1: Part1.A0, R1.leg2, R2.Pin_0
  N2: Part1.D8, MD03A1.2INb#142
  N3: Part1.D12/MISO, MD03A1.2INb#143
  N4: Part1.D2, MD03A1.1INa
  N5: Part1.D3_PWM, MD03A1.PWM
  N6: Part1.D5_PWM, MD03A1.2PWM
  N7: Part1.D7, MD03A1.1INb
  N8: M1.pin_1, MD03A1.OUT_1A
  N9: M1.pin_2, MD03A1.OUT_1B
  N10: M2.pin_1, MD03A1.OUT_2A
  N11: M2.pin_2, MD03A1.OUT_2B
  N12: R1.leg1, MD03A1.+5V_(IN)
  N13: R2.Pin_1, MD03A1.GND#136
  N14: MD03A1.VIN, U1.+
  N15: MD03A1.GND#151, U1.-
